# Fritzing sketch 4-digit-display-basic (saved by Fritzing 0.9.10b)

parts:
  Display1 = 4-Digit 7-segment LED Display [package=THT]
  Part1 = Arduino Uno (Rev3) - ICSP

nets:
  GND: Display1.GND, Part1.GND
  VCC: Display1.VCC, Part1.5V
  N1: Display1.DIO, Part1.D3_PWM
  N2: Display1.CLK, Part1.D2

custom parts:
  4-Digit 7-segment LED Display: A 4-digit 7-segments LED display PCB module driven by a TM1637 control IC via 1-wire protocol.
